# Fritzing sketch beaglecam-prototype (saved by Fritzing 0.9.8b)
breadboards: 1

parts:
  BeagleBone1 = BeagleBone Black
  Camera_Module = TRANSCHIPTC5747 [package=camera_sfv24r-2st_2]
  Arduino_Nano_33_BLE = Arduino Nano 33 BLE Sense
  PRU_Diag_LED = smd LED [color="Orange (620nm)" package="0805 [SMD]"]
  R1 = Resistor [tolerance=±5% resistance=470 power=0.25 package=THT]
  R2 = Resistor [tolerance=±5% resistance=10k power=0.25 package=THT]
  R3 = Resistor [tolerance=±5% resistance=10k power=0.25 package=THT]
  C2 = Ceramic Capacitor [capacitance=1µF voltage=35V package="0603 [SMD, multilayer]"]
  Midas_I2C_LCD = Midas 16x2 I2C LCD
  C1 = Ceramic Capacitor [capacitance=1µF voltage=35V package="0603 [SMD, multilayer]"]

nets:
  N1: BeagleBone1.P9_1_-_GND, Camera_Module.DOUT_1, Camera_Module.DOUT_5, R1.Pin_0
  N2: BeagleBone1.P9_3_-_3.3V, Camera_Module.DOUT_0, Camera_Module.DOUT_6, R2.Pin_0, R3.Pin_0
  N3: BeagleBone1.P9_10_-_Reset_button, Arduino_Nano_33_BLE.D2
  N4: BeagleBone1.P9_13_-_GPIO0_31/UART4-TX(6), Arduino_Nano_33_BLE.D4
  N5: BeagleBone1.P9_19_-_GPIO0_15/I2C2-SCL(3)/SPI1-CS1(4), Camera_Module.DOUT_7, R3.Pin_1
  N6: BeagleBone1.P9_20_-_GPIO0_14/I2C2-SDA(3)/SPI1-CS0(4), Camera_Module.DOUT_4, R2.Pin_1
  N7: BeagleBone1.P9_24_-_GPIO0_12/UART1-TX(0)/I2C1-SCL(3), Camera_Module.DOUT_3
  N8: BeagleBone1.P9_25_-_GPIO3_21, Camera_Module.PS1
  N9: BeagleBone1.P9_27_-_GPIO3_19, Camera_Module.CLK_IN
  N10: BeagleBone1.P9_29_-_GPIO3_15/SPI1-D0(3)/PWM0B(1), Camera_Module.RESET_N
  N11: BeagleBone1.P9_30_-_GPIO3_16/SPI1-D1(3), Camera_Module.PS2
  N12: BeagleBone1.P9_31_-_GPIO3_14/SPI1-SCLK(3)/PWM0A(1), Camera_Module.AVDD28
  N13: BeagleBone1.P9_41_-_GPIO0_20, Camera_Module.AGND
  N14: BeagleBone1.P9_42_-_GPIO0_7, Camera_Module.SHIELD
  N15: BeagleBone1.P8_7_-_GPIO2_2, Camera_Module.DOUT_2
  N16: BeagleBone1.P8_15_-_GPIO1_15, Camera_Module.VCLK_OUT
  N17: BeagleBone1.P8_16_-_GPIO1_14, Camera_Module.SDIN
  N18: BeagleBone1.P8_20_-_GPIO1_31, PRU_Diag_LED.anode
  N19: BeagleBone1.P8_21_-_GPIO1_30, Camera_Module.DOUT_8
  GND: Arduino_Nano_33_BLE.GND, Arduino_Nano_33_BLE.A7, Midas_I2C_LCD.VSS
  N20: Arduino_Nano_33_BLE.D11/MOSI, Arduino_Nano_33_BLE.+5V
  N21: Arduino_Nano_33_BLE.A5, Midas_I2C_LCD.SCL
  N22: Arduino_Nano_33_BLE.A4, Midas_I2C_LCD.SDA
  3V3: Arduino_Nano_33_BLE.3V3, Midas_I2C_LCD.VDD, Midas_I2C_LCD.RST, C1.0
  N23: PRU_Diag_LED.cathode, R1.Pin_1
  N24: C2.0, Midas_I2C_LCD.CAP1P
  N25: C2.1, Midas_I2C_LCD.CAP1N
  N26: Midas_I2C_LCD.VOUT, C1.1

custom parts:
  BeagleBone Black: BeagleBone Black rev. A5B
  Arduino Nano 33 BLE Sense: The Nano 33 BLE Sense (without headers) is Arduino’s 3.3V AI enabled board in the smallest available form factor: 45x18mm! The Arduino Nano 33 BLE Sense is a completely new board on a well-known form factor. It comes with a series of embedded sensors: 9 axis inertial sensor: what makes this board ideal for wearable devices humidity, and temperature sensor: to get highly accurate measurements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
  Midas 16x2 I2C LCD: Midas 16x2 I2C Alphanumeric LCD - MCCOG21605B6W-FPTLWI
